# Fritzing sketch prototype (saved by Fritzing 0.9.2b)
breadboards: 1

parts:
  Bauteil1 = Arduino Uno (Rev3)
  D2 = Rectifier Diode [part_number=1N4001 package="300 mil [THT]"]
  L2 = Solenoid
  R4 = Resistor [tolerance=±5% resistance=100k package=THT]
  M1 = DC Motor
  Q3 = Basic FET N-Channel [package="TO220 [THT]"]
  R5 = Resistor [tolerance=±5% resistance=680 package=THT]
  R6 = Resistor [tolerance=±5% resistance=100k package=THT]
  D3 = Rectifier Diode [part_number=1N4001 package="300 mil [THT]"]
  U1 = PCF8574 [package="DIP16 [THT]"]
  R7 = Resistor [tolerance=±5% resistance=10k package=THT]
  R8 = Resistor [tolerance=±5% resistance=10k package=THT]
  RHT1 = Humidity and Temperature Sensor RHT03
  Q2 = Basic FET N-Channel [package="TO220 [THT]"]
  C4 = Ceramic Capacitor [capacitance=100nF package="100 mil [THT, multilayer]"]
  R10 = Resistor [tolerance=±5% resistance=680 package=THT]
  Q4 = NPN-Transistor [package="SOT-23 [SMD]"]
  R12 = Resistor [tolerance=±5% resistance=100k package=THT]
  LED1 = LED - 3mm [color="Green (555nm)" package="3 mm [THT]"]
  R13 = Resistor [tolerance=±5% resistance=680 package=THT]
  Q5 = NPN-Transistor [package="SOT-23 [SMD]"]
  R14 = Resistor [tolerance=±5% resistance=10k package=THT]
  R15 = Resistor [tolerance=±5% resistance=10k package=THT]

nets:
  N1: Bauteil1.A4/SDA, U1.SDA, R7.Pin_1, Q5.1
  GND: Bauteil1.GND, Q3.source, R6.Pin_0, U1.A0, U1.A1, U1.A3, U1.GND, Q2.source, C4.0, Q4.2
  N2: Bauteil1.A5/SCL, U1.SCL, R8.Pin_1, RHT1.GND_2
  N3: Bauteil1.D2, R5.Pin_0, R6.Pin_1
  VCC: Bauteil1.5V, R4.Pin_0, U1.VCC, R7.Pin_0, R8.Pin_0, RHT1.Vcc, C4.1, R13.Pin_0, R15.Pin_0
  N4: Bauteil1.VIN, D2.cathode, L2.pin2, M1.pin_2, D3.cathode
  N5: D2.anode, L2.pin1, Q2.drain
  N6: R4.Pin_1, Q2.gate, R10.Pin_1
  N7: M1.pin_1, Q3.drain, D3.anode
  N8: Q3.gate, R5.Pin_1
  N9: U1.P0, R12.Pin_1
  N10: U1.P1, LED1.cathode, R14.Pin_1
  N11: RHT1.Data-signal, Q5.2, R15.Pin_1
  N12: R10.Pin_0, Q4.1
  N13: Q4.0, R12.Pin_0
  N14: LED1.anode, R13.Pin_1
  N15: Q5.0, R14.Pin_0
